// Logisim project Circuitos.circ as structural Verilog: 4 circuits, main circuit Ejercicio-01
module Ejercicio_01 (
  input  P,
  input  Q,
  input  NOT,
  input  in_4,
  input  in_5,
  output out_6,
  output out_7,
  output out_8
);

  wire transistor_1_out, transistor_3_out, transistor_7_out, transistor_13_out;

  Transistor #(.\type ("n")) transistor_1 (.in(1'b0), .out(transistor_1_out), .gate(P));
  Transistor transistor_2 (.in(1'b1), .out(transistor_1_out), .gate(P));
  Transistor #(.\type ("n")) transistor_3 (.in(1'b0), .out(transistor_3_out), .gate(transistor_1_out));
  Transistor #(.\type ("n")) transistor_4 (.in(1'b0), .out(transistor_3_out), .gate(Q));
  Transistor transistor_5 (.in(1'b1), .out(out_8), .gate(transistor_3_out));
  Transistor #(.\type ("n")) transistor_6 (.in(1'b0), .out(out_8), .gate(transistor_3_out));
  Transistor transistor_7 (.in(1'b1), .out(transistor_7_out), .gate(Q));
  Transistor transistor_8 (.in(transistor_7_out), .out(transistor_3_out), .gate(transistor_1_out));
  Transistor transistor_9 (.in(1'b1), .out(out_6), .gate(NOT));
  Transistor #(.\type ("n")) transistor_10 (.in(1'b0), .out(out_6), .gate(NOT));
  Transistor #(.\type ("n")) transistor_11 (.in(1'b0), .out(out_7), .gate(in_4));
  Transistor #(.\type ("n")) transistor_12 (.in(1'b0), .out(out_7), .gate(in_5));
  Transistor transistor_13 (.in(1'b1), .out(transistor_13_out), .gate(in_5));
  Transistor transistor_14 (.in(transistor_13_out), .out(out_7), .gate(in_4));

  // Notes on the sheet:
  //   P̅
  //   P̅ + Q
  //   Negamos P, luego concatenamos NOR con NOT y obtenemos un OR entre P̅ y Q
  //   NOR
endmodule

module Ejercicio_02 (
  input  P,
  input  Q,
  output P_____Q
);

  wire and_1_out, and_2_out;

  and and_1 (and_1_out, Q, P);
  and and_2 (and_2_out, ~Q, ~P);  // AND_Gate
  or or_1 (P_____Q, and_1_out, and_2_out);
endmodule

module Ejercicio_03 (
  input  x_1,
  input  x_2,
  input  y_1,
  input  y_2,
  output x____y
);

  wire and_1_out, and_2_out, and_3_out, and_4_out, and_5_out;

  and and_1 (and_1_out, x_1, x_2);
  and and_2 (and_2_out, x_1, ~y_1);  // AND_Gate
  and and_3 (and_3_out, x_1, ~y_2);  // AND_Gate
  and and_4 (and_4_out, x_2, ~y_1);  // AND_Gate
  and and_5 (and_5_out, ~y_2, ~y_1);  // AND_Gate
  or or_1 (x____y, and_1_out, and_2_out, and_3_out, and_4_out, and_5_out);

  // Notes on the sheet:
  //   x_1x_2
  //   x_1!y_1
  //   x_1!y_2
  //   x_2!y_1
  //   !y_1!y_2
endmodule

module Ejercicio_04 (
  input  x_1,
  input  x_2,
  input  y_1,
  input  y_2,
  output x___y,
  output x___y_2,
  output x___y_3
);

  wire Ig1_out, Ig2_out, Ig3_out, Ig4_out, Ma1_out, Ma2_out, Ma3_out, Me1_out, Me2_out, Me3_out;

  and Me1 (Me1_out, ~x_1, ~x_2, ~y_1, y_2);  // AND_Gate
  and Me2 (Me2_out, x_1, ~x_2, y_1, y_2);  // AND_Gate
  and Ma2 (Ma2_out, x_1, x_2, y_1, ~y_2);  // AND_Gate
  and Ma1 (Ma1_out, ~x_1, x_2, ~y_1, ~y_2);  // AND_Gate
  and Ig1 (Ig1_out, ~x_1, ~x_2, ~y_1, ~y_2);  // AND_Gate
  and Ig2 (Ig2_out, ~x_1, x_2, ~y_1, y_2);  // AND_Gate
  and Me3 (Me3_out, ~x_1, y_1);  // AND_Gate
  and Ma3 (Ma3_out, x_1, ~y_1);  // AND_Gate
  and Ig3 (Ig3_out, x_1, ~x_2, y_1, ~y_2);  // AND_Gate
  and Ig4 (Ig4_out, x_1, x_2, y_1, y_2);
  or or_1 (x___y, Me3_out, Me2_out, Me1_out);
  or or_2 (x___y_2, Ma3_out, Ma2_out, Ma1_out);
  or or_3 (x___y_3, Ig4_out, Ig3_out, Ig2_out, Ig1_out);
endmodule
