// Logisim project Practica-03.circ as structural Verilog
module Ejercicio_02 (
  input  P,
  input  Q,
  output P_____Q
);

  wire and_1_out, and_2_out;

  and and_1 (and_1_out, Q, P);
  and and_2 (and_2_out, ~Q, ~P);  // AND_Gate
  or or_1 (P_____Q, and_1_out, and_2_out);
endmodule

module Ejercicio_03 (
  input  x_1,
  input  x_2,
  input  y_1,
  input  y_2,
  output x____y
);

  wire and_1_out, and_2_out, and_3_out, and_4_out, and_5_out;

  and and_1 (and_1_out, x_1, x_2);
  and and_2 (and_2_out, x_1, ~y_1);  // AND_Gate
  and and_3 (and_3_out, x_1, ~y_2);  // AND_Gate
  and and_4 (and_4_out, x_2, ~y_1);  // AND_Gate
  and and_5 (and_5_out, ~y_2, ~y_1);  // AND_Gate
  or or_1 (x____y, and_1_out, and_2_out, and_3_out, and_4_out, and_5_out);

  // Notes on the sheet:
  //   x_1x_2
  //   x_1!y_1
  //   x_1!y_2
  //   x_2!y_1
  //   !y_1!y_2
endmodule
