// Logisim project Circuitos.circ as structural Verilog: 5 circuits, main circuit Ejercicio-02
// C_2
module Complemento_a_2 (
  input  [7:0] A,
  output [7:0] C_2,
  output C_out
);

  wire [7:0] not_1_out;

  assign not_1_out = ~A;  // NOT_Gate not_1, 8 bits wide
  Ejercicio_03 ejercicio_03_1 (.A(not_1_out), .B(8'h1), .Resultado(C_2), .C_out(C_out));
endmodule

module Ejercicio_02 (
  input  C_in,
  input  A,
  input  B,
  output O,
  output C_out
);

  wire and_1_out, and_2_out, xor_1_out;

  xor xor_1 (xor_1_out, A, B);
  and and_1 (and_1_out, B, A);
  xor xor_2 (O, C_in, xor_1_out);
  and and_2 (and_2_out, xor_1_out, C_in);
  or or_1 (C_out, and_1_out, and_2_out);
endmodule

// Add8b
module Ejercicio_03 (
  input  [7:0] A,
  input  [7:0] B,
  output [7:0] Resultado,
  output C_out
);

  wire Sumador_1_c_out, Sumador_2_c_out, Sumador_3_c_out, Sumador_4_c_out, Sumador_5_c_out, Sumador_6_c_out,
       Sumador_7_c_out;

  Ejercicio_02 Sumador_1 (.C_in(1'b0), .A(A[0]), .B(B[0]), .O(Resultado[0]), .C_out(Sumador_1_c_out));
  Ejercicio_02 Sumador_2 (.C_in(Sumador_1_c_out), .A(A[1]), .B(B[1]), .O(Resultado[1]), .C_out(Sumador_2_c_out));
  Ejercicio_02 Sumador_3 (.C_in(Sumador_2_c_out), .A(A[2]), .B(B[2]), .O(Resultado[2]), .C_out(Sumador_3_c_out));
  Ejercicio_02 Sumador_4 (.C_in(Sumador_3_c_out), .A(A[3]), .B(B[3]), .O(Resultado[3]), .C_out(Sumador_4_c_out));
  Ejercicio_02 Sumador_5 (.C_in(Sumador_4_c_out), .A(A[4]), .B(B[4]), .O(Resultado[4]), .C_out(Sumador_5_c_out));
  Ejercicio_02 Sumador_6 (.C_in(Sumador_5_c_out), .A(A[5]), .B(B[5]), .O(Resultado[5]), .C_out(Sumador_6_c_out));
  Ejercicio_02 Sumador_7 (.C_in(Sumador_6_c_out), .A(A[6]), .B(B[6]), .O(Resultado[6]), .C_out(Sumador_7_c_out));
  Ejercicio_02 Sumador_8 (.C_in(Sumador_7_c_out), .A(A[7]), .B(B[7]), .O(Resultado[7]), .C_out(C_out));
endmodule

// ALU
module Ejercicio_04 (
  input  [7:0] A,
  input  [7:0] B,
  input  Op,
  output [7:0] Resultado
);

  wire [7:0] complemento_a_2_1_c_2, ejercicio_03_1_resultado, ejercicio_03_2_resultado;

  Complemento_a_2 complemento_a_2_1 (.A(B), .C_2(complemento_a_2_1_c_2));  // open: C_out
  Ejercicio_03 ejercicio_03_1 (.A(A), .B(B), .Resultado(ejercicio_03_1_resultado));  // open: C_out
  Ejercicio_03 ejercicio_03_2 (.A(A), .B(complemento_a_2_1_c_2), .Resultado(ejercicio_03_2_resultado));  // open: C_out
  Multiplexer #(.width(8), .enable("false")) multiplexer_1 (
    .in0(ejercicio_03_1_resultado), .in1(ejercicio_03_2_resultado), .out(Resultado), .sel(Op));
endmodule

// Multiplicador
module Ejercicio_05 (
  input  [7:0] A,
  input  in_2,
  input  [7:0] B,
  input  in_4,
  output [7:0] out_5
);

  wire [7:0] complemento_a_2_1_c_2, complemento_a_2_2_c_2, ejercicio_04_1_resultado,
       ejercicio_04_2_resultado, ejercicio_04_3_resultado, ejercicio_04_4_resultado,
       ejercicio_04_5_resultado, ejercicio_04_6_resultado, multiplexer_1_out, multiplexer_2_out,
       transistor_1_out, transistor_3_out, transistor_5_out, transistor_7_out, transistor_9_out,
       transistor_11_out, transistor_13_out, transistor_15_out;

  Complemento_a_2 complemento_a_2_1 (.A(A), .C_2(complemento_a_2_1_c_2));  // open: C_out
  Multiplexer #(.width(8), .enable("false")) multiplexer_1 (
    .in0(A), .in1(complemento_a_2_1_c_2), .out(multiplexer_1_out), .sel(in_2));
  Multiplexer #(.width(8), .enable("false")) multiplexer_2 (
    .in0(B), .in1(complemento_a_2_2_c_2), .out(multiplexer_2_out), .sel(in_4));
  Complemento_a_2 complemento_a_2_2 (.A(B), .C_2(complemento_a_2_2_c_2));  // open: C_out
  Transistor #(.\type ("n"), .gate("br"), .width(8)) transistor_1 (
    .in(multiplexer_1_out), .out(transistor_1_out), .gate(multiplexer_2_out[0]));
  Transistor #(.gate("br"), .width(8)) transistor_2 (
    .in({8{1'b0}}), .out(transistor_1_out), .gate(multiplexer_2_out[0]));
  Transistor #(.gate("br"), .width(8)) transistor_3 (
    .in({8{1'b0}}), .out(transistor_3_out), .gate(multiplexer_2_out[1]));
  Transistor #(.\type ("n"), .gate("br"), .width(8)) transistor_4 (
    .in({multiplexer_1_out[6:0], 1'b0}), .out(transistor_3_out), .gate(multiplexer_2_out[1]));
  Transistor #(.\type ("n"), .gate("br"), .width(8)) transistor_5 (
    .in({multiplexer_1_out[5:0], 2'b00}), .out(transistor_5_out), .gate(multiplexer_2_out[2]));
  Transistor #(.gate("br"), .width(8)) transistor_6 (
    .in({8{1'b0}}), .out(transistor_5_out), .gate(multiplexer_2_out[2]));
  Transistor #(.gate("br"), .width(8)) transistor_7 (
    .in({8{1'b0}}), .out(transistor_7_out), .gate(multiplexer_2_out[3]));
  Transistor #(.\type ("n"), .gate("br"), .width(8)) transistor_8 (
    .in({multiplexer_1_out[4:0], 3'b000}), .out(transistor_7_out), .gate(multiplexer_2_out[3]));
  Transistor #(.\type ("n"), .gate("br"), .width(8)) transistor_9 (
    .in({multiplexer_1_out[3:0], 4'b0000}), .out(transistor_9_out), .gate(multiplexer_2_out[4]));
  Transistor #(.gate("br"), .width(8)) transistor_10 (
    .in({8{1'b0}}), .out(transistor_9_out), .gate(multiplexer_2_out[4]));
  Transistor #(.\type ("n"), .gate("br"), .width(8)) transistor_11 (
    .in({multiplexer_1_out[2:0], {5{1'b0}}}), .out(transistor_11_out), .gate(multiplexer_2_out[5]));
  Transistor #(.gate("br"), .width(8)) transistor_12 (
    .in({8{1'b0}}), .out(transistor_11_out), .gate(multiplexer_2_out[5]));
  Transistor #(.gate("br"), .width(8)) transistor_13 (
    .in({8{1'b0}}), .out(transistor_13_out), .gate(multiplexer_2_out[6]));
  Transistor #(.\type ("n"), .gate("br"), .width(8)) transistor_14 (
    .in({multiplexer_1_out[1:0], {6{1'b0}}}), .out(transistor_13_out), .gate(multiplexer_2_out[6]));
  Transistor #(.gate("br"), .width(8)) transistor_15 (
    .in({8{1'b0}}), .out(transistor_15_out), .gate(multiplexer_2_out[7]));
  Transistor #(.\type ("n"), .gate("br"), .width(8)) transistor_16 (
    .in({multiplexer_1_out[0], {7{1'b0}}}), .out(transistor_15_out), .gate(multiplexer_2_out[7]));
  Ejercicio_04 ejercicio_04_1 (
    .A(transistor_1_out), .B(transistor_3_out), .Op(1'b0), .Resultado(ejercicio_04_1_resultado));
  Ejercicio_04 ejercicio_04_2 (
    .A(ejercicio_04_1_resultado), .B(transistor_5_out), .Op(1'b0), .Resultado(ejercicio_04_2_resultado));
  Ejercicio_04 ejercicio_04_3 (
    .A(ejercicio_04_2_resultado), .B(transistor_7_out), .Op(1'b0), .Resultado(ejercicio_04_3_resultado));
  Ejercicio_04 ejercicio_04_4 (
    .A(ejercicio_04_3_resultado), .B(transistor_9_out), .Op(1'b0), .Resultado(ejercicio_04_4_resultado));
  Ejercicio_04 ejercicio_04_5 (
    .A(ejercicio_04_4_resultado), .B(transistor_11_out), .Op(1'b0), .Resultado(ejercicio_04_5_resultado));
  Ejercicio_04 ejercicio_04_6 (
    .A(ejercicio_04_5_resultado), .B(transistor_13_out), .Op(1'b0), .Resultado(ejercicio_04_6_resultado));
  Ejercicio_04 ejercicio_04_7 (.A(ejercicio_04_6_resultado), .B(transistor_15_out), .Op(1'b0), .Resultado(out_5));
endmodule
