// Logisim project Circuitos.circ as structural Verilog: 4 circuits, main circuit Ejercicio-01
module Ejercicio_01 (
  input  in_1,
  input  in_2
);

  wire A_qn, and_1_out, and_2_out, and_3_out, B_qn, clock_1_out, not_1_out;
  wire [1:0] B_q;

  not not_1 (not_1_out, in_1);
  and and_1 (and_1_out, A_qn, B_q[0], not_1_out);
  and and_2 (and_2_out, not_1_out, B_q[0], B_q[1]);
  Clock clock_1 (.out(clock_1_out));
  and and_3 (and_3_out, not_1_out, B_qn);
  S_R_Flip_Flop A (.S(and_1_out), .clk(clock_1_out), .R(and_2_out), .Q(B_q[1]), .Qn(A_qn));  // open: preset, reset, en
  S_R_Flip_Flop B (.S(and_3_out), .clk(clock_1_out), .R(B_q[0]), .Q(B_q[0]), .Qn(B_qn));  // open: preset, reset, en
  Hex_Digit_Display hex_digit_display_1 (.value({{2{in_2}}, B_q}));  // open: dp
endmodule

module Ejercicio_02 (
  input  Reloj,
  input  Enable,
  input  [7:0] Entrada,
  input  Pin_0,
  output [7:0] Salida
);

  D_Flip_Flop d_ff_1 (.clk(Reloj), .D(Entrada[0]), .Q(Salida[0]), .en(Enable), .reset(Pin_0));  // open: Qn, preset
  D_Flip_Flop d_ff_2 (.clk(Reloj), .D(Entrada[1]), .Q(Salida[1]), .en(Enable), .reset(Pin_0));  // open: Qn, preset
  D_Flip_Flop d_ff_3 (.clk(Reloj), .D(Entrada[2]), .Q(Salida[2]), .en(Enable), .reset(Pin_0));  // open: Qn, preset
  D_Flip_Flop d_ff_4 (.clk(Reloj), .D(Entrada[3]), .Q(Salida[3]), .en(Enable), .reset(Pin_0));  // open: Qn, preset
  D_Flip_Flop d_ff_5 (.clk(Reloj), .D(Entrada[4]), .Q(Salida[4]), .en(Enable), .reset(Pin_0));  // open: Qn, preset
  D_Flip_Flop d_ff_6 (.clk(Reloj), .D(Entrada[5]), .Q(Salida[5]), .en(Enable), .reset(Pin_0));  // open: Qn, preset
  D_Flip_Flop d_ff_7 (.clk(Reloj), .D(Entrada[6]), .Q(Salida[6]), .en(Enable), .reset(Pin_0));  // open: Qn, preset
  D_Flip_Flop d_ff_8 (.clk(Reloj), .D(Entrada[7]), .Q(Salida[7]), .en(Enable), .reset(Pin_0));  // open: Qn, preset
endmodule

module Ejercicio_03 (
  input  Clock,
  input  Pin_0,
  input  [1:0] LR1,
  input  [7:0] Escribir_Datos,
  input  Escribir,
  input  [1:0] LR2,
  input  [1:0] Escribir_Registro,
  output [7:0] R1,
  output [7:0] R2,
  output [7:0] Leer_Datos_1,
  output [7:0] Leer_Datos_2,
  output [7:0] R3,
  output [7:0] R4
);

  wire and_1_out, and_2_out, and_3_out, and_4_out, demultiplexer_1_out0, demultiplexer_1_out1,
       demultiplexer_1_out2, demultiplexer_1_out3;

  Demultiplexer #(.select(2), .enable("false")) demultiplexer_1 (
    .out0(demultiplexer_1_out0), .out1(demultiplexer_1_out1), .out2(demultiplexer_1_out2),
    .out3(demultiplexer_1_out3), .in(1'b1), .sel(Escribir_Registro));
  and and_1 (and_1_out, Escribir, demultiplexer_1_out0);
  and and_2 (and_2_out, Escribir, demultiplexer_1_out1);
  and and_3 (and_3_out, Escribir, demultiplexer_1_out2);
  and and_4 (and_4_out, Escribir, demultiplexer_1_out3);
  Ejercicio_02 ejercicio_02_1 (.Reloj(Clock), .Entrada(Escribir_Datos), .Pin_0(Pin_0), .Salida(R1), .Enable(and_1_out));
  Ejercicio_02 ejercicio_02_2 (.Reloj(Clock), .Entrada(Escribir_Datos), .Pin_0(Pin_0), .Salida(R2), .Enable(and_2_out));
  Ejercicio_02 ejercicio_02_3 (.Reloj(Clock), .Entrada(Escribir_Datos), .Pin_0(Pin_0), .Salida(R3), .Enable(and_3_out));
  Ejercicio_02 ejercicio_02_4 (.Reloj(Clock), .Entrada(Escribir_Datos), .Pin_0(Pin_0), .Salida(R4), .Enable(and_4_out));
  Multiplexer #(.select(2), .width(8)) multiplexer_1 (
    .in0(R1), .in1(R2), .in2(R3), .in3(R4), .out(Leer_Datos_1), .sel(LR1));  // open: en
  Multiplexer #(.select(2), .width(8)) multiplexer_2 (
    .in0(R1), .in1(R2), .in2(R3), .in3(R4), .out(Leer_Datos_2), .sel(LR2));  // open: en

  // Notes on the sheet:
  //   4  Registros
  //   Leer Registros 1
  //   Leer Resgitros 2
endmodule

module Ejercicio_04 (
  input  Clock,
  input  Pin,
  input  [7:0] in_3,
  input  [7:0] Inmediato,
  input  in_5,
  input  Escribir,
  input  [1:0] Leer_Registro_1,
  input  [1:0] Escribir_registro,
  input  in_9,
  input  [1:0] Leer_Registro_2,
  input  in_11,
  output [7:0] out_12,
  output [7:0] Registro_1,
  output [7:0] Registro_2,
  output [7:0] Registro_3,
  output [7:0] Registro_4
);

  wire [7:0] adder_1_out, ejercicio_03_1_leer_datos_1, ejercicio_03_1_leer_datos_2, multiplexer_1_out,
       multiplexer_2_out, subtractor_1_out;

  Multiplexer #(.width(8)) multiplexer_1 (.in0(in_3), .in1(out_12), .out(multiplexer_1_out), .sel(in_9));  // open: en
  Ejercicio_03 ejercicio_03_1 (
    .Escribir_Datos(multiplexer_1_out), .Escribir(Escribir), .Escribir_Registro(Escribir_registro),
    .Clock(Clock), .Pin_0(Pin), .R1(Registro_1), .R2(Registro_2), .Leer_Datos_1(ejercicio_03_1_leer_datos_1),
    .LR1(Leer_Registro_1), .Leer_Datos_2(ejercicio_03_1_leer_datos_2), .R3(Registro_3),
    .LR2(Leer_Registro_2), .R4(Registro_4));
  Multiplexer #(.width(8)) multiplexer_2 (
    .in0(ejercicio_03_1_leer_datos_2), .in1(Inmediato), .out(multiplexer_2_out), .sel(in_11));  // open: en
  Adder adder_1 (.a(ejercicio_03_1_leer_datos_1), .b(multiplexer_2_out), .out(adder_1_out));  // open: cin, cout
  Subtractor subtractor_1 (
    .a(ejercicio_03_1_leer_datos_1), .b(multiplexer_2_out), .out(subtractor_1_out));  // open: bin, bout
  Multiplexer #(.width(8)) multiplexer_3 (
    .in0(adder_1_out), .in1(subtractor_1_out), .out(out_12), .sel(in_5));  // open: en
endmodule
